# Fritzing sketch projecizimi (saved by Fritzing 0.9.3b)

parts:
  Parça1 = Arduino Mega 2560 (Rev3)
  Parça2 = DeuLigne 1.1 - The Snootlab's LCD shield for Arduino
  hc-sr1 = hc-sr04
  RHT1 = Humidity and Temperature Sensor RHT03
  M1 = DC Motor
  J1 = Piezo Speaker
  U1 = 2-Channel 5v Relay Shield [package=relay-2ch5v10a]
  VCC2 = Battery
  VCC3 = Battery

nets:
  N1: Parça1.D21/SCL, RHT1.GND_1
  N2: Parça1.D20/SDA, RHT1.GND_2
  5V: Parça1.5V, hc-sr1.VCC
  N3: Parça1.D32, hc-sr1.Trig
  N4: Parça1.D33, hc-sr1.Echo
  N5: Parça1.D50, U1.IN1
  N6: Parça1.D51, U1.IN2
  GND: Parça1.GND, U1.GND
  +5V: Parça2.+5V, U1.VCC
  GND_2: Parça2.GND, hc-sr1.GND, RHT1.Data-signal
  VIN: Parça2.VIN, RHT1.Vcc
  N7: M1.pin_1, U1.K2-In
  N8: J1.pin1, U1.K1-In
  N9: U1.K1-On, VCC2.-
  N10: U1.K2-On, VCC3.-

custom parts:
  2-Channel 5v Relay Shield: 2 Channel 5v Relay Shield w. 2x SPD-06VDC-SD-C
